# Fritzing sketch opto (saved by Fritzing 0.9.3b)
circuit board: 8.46667cm x 5.64444cm
breadboards: 1

parts:
  U1 = ESP8266 WiFi Module [part_number=ESP8266]
  U2 = Sharp PC817 [package=THT]
  S2 = Reed switch [package=THT]
  R2 = Resistor [tolerance=±5% resistance=100 package="2010 [SMD]"]
  D1 = Rectifier Diode [part_number=1N4001 package="Melf DO-213 AB [SMD]"]
  R3 = Resistor [tolerance=±5% resistance=470 package="2010 [SMD]"]
  C1 = Ceramic Capacitor [capacitance=100nF package="100 mil [THT, multilayer]"]
  R4 = Resistor [tolerance=±5% resistance=10k package="2010 [SMD]"]
  JP1 = Header 2 [package=screwterminal-3.5mm-2_lock]
  JP2 = Header 3 [package=screwterminal-3.5mm-3_lock.007s]

nets:
  N1: U1.VCC, S2.pin_2
  N2: U1.GND, U2.Pin_2, C1.0, R4.Pin_1, JP2.3
  N3: U1.GPIO_5, R2.Pin_1, D1.cathode, R3.Pin_0, C1.1, JP2.2
  N4: U2.Pin_1, R2.Pin_0
  N5: U2.Pin_4, JP1.1
  N6: U2.Pin_3, JP1.2
  N7: S2.pin_1, D1.anode, R3.Pin_1, R4.Pin_0, JP2.1
